# Fritzing sketch Electronic2 (saved by Fritzing 0.9.2b)

parts:
  Composant1 = Arduino Nano (Rev3.0)
  U2 = RF-LINK_TX [package=rf-link_tx]
  Composant2 = KY-033 Tracing Black White Line Hunting Sensor Module For Arduino
  Composant4 = BMP180 Breakout (GY-68)
  DHT1 = DHT11 Humitidy and Temperature Sensor
  R1 = Resistor [tolerance=±20% resistance=4.7k package=THT]
  Q1 = NPN-Transistor [package="TO92 [THT]"]
  R2 = Resistor [tolerance=±20% resistance=10k package=THT]
  Q2 = NPN-Transistor [package="TO92 [THT]"]
  U3 = LIPO-2000mAh [package=lipo-2000]
  U5 = mystery part, 4 pins [chip_label=LM2596]
  U4 = mystery part, 6 pins [chip_label=TP4056]
  M1 = DC Motor
  R3 = Resistor [tolerance=±20% resistance=20k package=THT]
  R4 = PHOTOCELL [package=photocell-kit]
  R5 = Resistor [tolerance=±20% resistance=10k package=THT]

nets:
  N1: Composant1.D3, Composant2.S
  N2: Composant1.D4, Q2.C
  N3: Composant1.D5, Q1.C
  N4: Composant1.D7, U2.DATA
  N5: Composant1.D9, DHT1.DATA, R1.Pin_1
  N6: Composant1.VIN, U4.pin1
  N7: Composant1.GND, U4.pin2
  N8: Composant1.A3, R4.P$1, R5.Pin_1
  N9: Composant1.A2, Composant4.SCL
  N10: Composant1.A1, Composant4.SDA
  N11: Composant2.GND, Q2.E
  N12: Composant4.VCC, R2.Pin_0, R3.Pin_1
  N13: Composant4.GND, Q1.E
  N14: U3.+, U4.pin3
  N15: U3.-, U4.pin4
  N16: U5.pin1, M1.pin_2
  N17: U5.pin3, U4.pin6
  N18: U5.pin4, U4.pin5

notes:
  DHT
  RF 433 Mhz
  Emitter
  Air pressure sensor (soon)
  Tachometer
  LM2596 - Adjustable Mini DC-DC step-down Module
  Dynamo
  TP4056 - Lithium battery charging and protection module
  Batterie Lithium Ion polymer - 3.7V 2200 mAh (compatible 2A)
  3.3V
  Photo

custom parts:
  RF-LINK_TX: Common RF transmitter of the 315.00Mhz varity
  KY-033 Tracing Black White Line Hunting Sensor Module For Arduino: Tracing Black White Line Hunting Sensor Module For Arduino Description: This is KY-033 tracking sensor. The KY-033 measures the intensity of infrared radiation and delivers it as an analog output voltage. Features: Operating voltage: 2.5 - 12V(cannot over12V) working current: 18mA-20mA at 5V Enhanced accuracy Documents: http://www.vishay.com/docs/83760/tcrt5000.pdf
  BMP180 Breakout (GY-68): This is a simple breakout board for the BMP180, a high-precision, low-power barometric pressure sensor made by Bosch Sensortec. The range of measurement is from 300hPa to 1100hPa. The sensor can be supplied with voltage ranging from 1.8V to 3.6V. Operating temperature range is -40 to +85 °C. This particular breakout board (or perhaps the configuration) is produced by Shenzhen Keep Power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
  DHT11 Humitidy and Temperature Sensor: DHT11 Humidity and Temperature Sensor

// code stored in the sketch: RF Transmitter and Reseiver mine.ino

/*
   Transmitter 
*/
#include <Manchester.h>

  #define TX_PIN 0  //(5 attiny85)pin where your transmitter is connected
  #define led_PIN 1 //(6 attiny85)
  const int button_PIN = A1; //(7 attiny85)
  const int threshold = 800;
  
  #define button_PIN1 A3 //(2 attiny85)
  //const int threshold1 = 800;
  uint16_t transmit_data = 2761;
  uint16_t transmit_data1 = 0000;
  void setup() {
    pinMode(led_PIN, OUTPUT);
    pinMode(button_PIN, INPUT);
    digitalWrite(button_PIN,LOW);
    pinMode(button_PIN1, INPUT);
    digitalWrite(button_PIN1,LOW);
  man.setupTransmit(TX_PIN, MAN_1200);
  
  } 
void loop() {
 int analogValue = analogRead(button_PIN);
  
  if (analogValue > threshold) {
    digitalWrite(led_PIN, HIGH);
    man.transmit(transmit_data);
  } 
  else {
    digitalWrite(led_PIN,LOW); 
  }
//  int analogValue = analogRead(button_PIN1);
  
  if (analogValue < threshold) {
    digitalWrite(led_PIN, HIGH);
    man.transmit(transmit_data1);
  } 
  else {
    digitalWrite(led_PIN,LOW);}  
 
  
}

/*....................................................................




/*
   Receiver 
*/
#include <Manchester.h>

#define RX_PIN 4 
#define led_PIN 7
#define led1_PIN 8
#define Relay_PIN 10
uint8_t moo = 1;
uint8_t data1;
#define BUFFER_SIZE 10
uint8_t buffer[BUFFER_SIZE];

int incomingData = 0;   // for incoming serial data

void setup()


{
 
pinMode(RX_PIN, INPUT);  
pinMode(led_PIN, OUTPUT);
pinMode(led1_PIN, OUTPUT);
digitalWrite(led_PIN, moo);
pinMode(Relay_PIN, OUTPUT);
  man.setupReceive(RX_PIN, MAN_1200);
  man.beginReceiveArray(BUFFER_SIZE, buffer);
  man.beginReceive();
  
    Serial.begin(9600);  
   //Serial.println( "Receiver is ON" );
  
}

void loop() {
  if (man.receiveComplete()) {
    uint8_t receivedSize = 0;
    
    digitalWrite(Relay_PIN,LOW);
    //digitalWrite(led_PIN,LOW);
    
    incomingData = Serial.read();
    //Serial.print("I received: ");
    Serial.println(incomingData, DEC);
    
    
    man.beginReceiveArray(BUFFER_SIZE, buffer); //start listening for next message 
    moo = ++moo % 2;
    digitalWrite(led_PIN, moo);
    
    digitalWrite(Relay_PIN,HIGH);
    //incomingData = Serial.read();
    //Serial.println(incomingData, DEC);
    Serial.println("data1");
     }
     if (man.receiveComplete()) {
    uint16_t m = man.getMessage();
    digitalWrite(Relay_PIN,LOW);
    man.beginReceive(); //start listening for next message right after you retrieve the message
    moo = ++moo % 2;
    digitalWrite(led1_PIN, moo);
    Serial.println(2761);
    data1 = ++data1 % 2;
   digitalWrite(Relay_PIN,HIGH);
     }  

}
